# Fritzing sketch Joystick2 (saved by Fritzing 0.9.10b)
breadboards: 1

parts:
  U1 = 74HC595 [package="DIP16 [THT]"]
  LED1 = smd LED [color="Blue (430nm)" part_number="LED 1" package="1206 [SMD]"]
  LED2 = smd LED [color="Yellow (585nm)" part_number="LED 2" package="1206 [SMD]"]
  LED3 = smd LED [color="Blue (430nm)" package="1206 [SMD]"]
  LED4 = smd LED [color="Yellow (585nm)" package="1206 [SMD]"]
  LED5 = smd LED [color="Blue (430nm)" package="1206 [SMD]"]
  LED6 = smd LED [color="Yellow (585nm)" package="1206 [SMD]"]
  LED7 = smd LED [color="Blue (430nm)" package="1206 [SMD]"]
  LED8 = smd LED [color="Yellow (585nm)" package="1206 [SMD]"]
  Part1 = Thumb Joystick
  Part2 = Arduino Uno (Rev3)
  R14 = Resistor [tolerance=±5% power=0.25 resistance=220 package=THT]
  R15 = Resistor [tolerance=±5% power=0.25 resistance=220 package=THT]
  R16 = Resistor [tolerance=±5% power=0.25 resistance=220 package=THT]
  R17 = Resistor [tolerance=±5% power=0.25 resistance=220 package=THT]
  R18 = Resistor [tolerance=±5% power=0.25 resistance=220 package=THT]
  R19 = Resistor [tolerance=±5% power=0.25 resistance=220 package=THT]
  R22 = Resistor [tolerance=±5% power=0.25 resistance=220 package=THT]
  R23 = Resistor [tolerance=±5% power=0.25 resistance=220 package=THT]

nets:
  N1: U1.Q1, R22.Pin_0
  N2: U1.Q2, R23.Pin_0
  N3: U1.Q3, R15.Pin_0
  N4: U1.Q4, R16.Pin_0
  N5: U1.Q5, R17.Pin_0
  N6: U1.Q6, R18.Pin_0
  N7: U1.Q7, R19.Pin_0
  GND: U1.GND, U1.OE, LED1.cathode, LED2.cathode, LED3.cathode, LED4.cathode, LED5.cathode, LED6.cathode, LED7.cathode, LED8.cathode, Part1.GND, Part2.GND
  VCC: U1.MR, U1.VCC, Part1.VCC, Part2.5V
  N8: U1.SH_CP, Part2.D9_PWM
  N9: U1.ST_CP, Part2.D10_PWM/SS
  N10: U1.DS, Part2.D8
  N11: U1.Q0, R14.Pin_0
  N12: LED1.anode, R14.Pin_1
  N13: LED2.anode, R22.Pin_1
  N14: LED3.anode, R23.Pin_1
  N15: LED4.anode, R15.Pin_1
  N16: LED5.anode, R16.Pin_1
  N17: LED6.anode, R17.Pin_1
  N18: LED7.anode, R18.Pin_1
  N19: LED8.anode, R19.Pin_1
  N20: Part1.SEL, Part2.D4
  N21: Part1.HORZ, Part2.A0
  N22: Part1.VERT, Part2.A1
