# Fritzing sketch Buttons (saved by Fritzing 1.0.6)
breadboards: 1

parts:
  R1 = Vertical Resistor [tolerance=±5% resistance=1k package=THT]
  R2 = Vertical Resistor [tolerance=±5% resistance=1k package=THT]
  LED1 = LED Red 3mm - Top [color="Blue (430nm)" package="3 mm [THT] Top"]
  R3 = Vertical Resistor [tolerance=±5% resistance=1k package=THT]
  Part1 = Freenove ESP32 GPIO Extension
  Part2 = Freenove ESP32 WROVER [package=ESP32-WROVER]  # not connected
  S2 = Pushbutton [package="[THT]"]
  S3 = Pushbutton [package="[THT]"]

nets:
  N1: R1.Pin_0, R2.Pin_0, Part1.GND, Part1.pin_82, Part1.pin_85, Part1.pin_86, Part1.pin_89
  N2: R1.Pin_1, Part1.25, S2.Pin_1, S2.Pin_2
  N3: R2.Pin_1, Part1.26, S3.Pin_1, S3.Pin_2
  N4: LED1.cathode, Part1.pin_87, Part1.pin_88
  N5: LED1.anode, R3.Pin_0
  N6: R3.Pin_1, Part1.27
  N7: Part1.5V, Part1.pin_83, Part1.pin_84, S2.Pin_3, S2.Pin_4, S3.Pin_3, S3.Pin_4

custom parts:
  Vertical Resistor: A generic resistor (0.25W)
  LED Red 3mm - Top: A generic red LED (~1.8V)
  Freenove ESP32 GPIO Extension: WS2812B_8_LED_Ring
