# Fritzing sketch MovinWDC2 (saved by Fritzing 1.0.6)
breadboards: 1

parts:
  Part1 = Freenove ESP32 GPIO Extension
  Part2 = Freenove ESP32 WROVER [package=ESP32-WROVER]  # not connected
  IC1 = L293D [package=THT]
  M1 = DC Motor [voltage_(max)=6V voltage_(min)=3V]

nets:
  N1: Part1.14, IC1.In_2
  N2: Part1.12, IC1.In_1
  N3: Part1.GND, Part1.pin_82, Part1.pin_85, Part1.pin_86, Part1.pin_89, IC1.0V
  N4: Part1.13, IC1.Enable_1
  N5: Part1.5V, Part1.pin_83, Part1.pin_84, IC1.+Vmotor, IC1.+V
  N6: Part1.pin_87, Part1.pin_88
  N7: IC1.Out_1_(_Controlled_by_Enable_1_), M1.pin_1
  N8: IC1.Out_2_(_Controlled_by_Enable_1_), M1.pin_2

custom parts:
  Freenove ESP32 GPIO Extension: WS2812B_8_LED_Ring
