# Fritzing sketch DC Motor III (saved by Fritzing 1.0.6)
breadboards: 1

parts:
  IC1 = L293D [package=THT]
  M1 = DC Motor [voltage_(max)=6V voltage_(min)=3V]
  Part1 = Freenove ESP32 GPIO Extension
  Part2 = Freenove ESP32 WROVER [package=ESP32-WROVER]  # not connected
  S4 = Pushbutton [package="[THT]"]
  S5 = Pushbutton [package="[THT]"]
  R5 = Vertical Resistor [tolerance=±5% resistance=1k package=THT]
  R6 = Vertical Resistor [tolerance=±5% resistance=1k package=THT]
  LED1 = LED Red 3mm - Top [color="Red (633nm)" package="3 mm [THT] Top"]
  LED2 = LED Red 3mm - Top [color="Blue (430nm)" package="3 mm [THT] Top"]
  R7 = Vertical Resistor [tolerance=±5% resistance=220 package=THT]
  R8 = Vertical Resistor [tolerance=±5% resistance=220 package=THT]

nets:
  N1: IC1.Enable_1, Part1.23#39
  N2: IC1.In_1, Part1.32
  N3: IC1.Out_1_(_Controlled_by_Enable_1_), M1.pin_1
  N4: IC1.0V, Part1.GND, Part1.pin_82, Part1.pin_85, Part1.pin_86, Part1.pin_89, R5.Pin_1, R6.Pin_1, LED1.cathode, LED2.cathode
  N5: IC1.Out_2_(_Controlled_by_Enable_1_), M1.pin_2
  N6: IC1.In_2, Part1.23#8
  N7: IC1.+Vmotor, IC1.+V, Part1.5V, Part1.pin_83, Part1.pin_84
  N8: Part1.14, R8.Pin_0
  N9: Part1.pin_87, Part1.pin_88, S4.Pin_3, S4.Pin_4, S5.Pin_3, S5.Pin_4
  N10: S4.Pin_1, S4.Pin_2, R5.Pin_0
  N11: S5.Pin_1, S5.Pin_2, R6.Pin_0
  N12: LED1.anode, R8.Pin_1
  N13: LED2.anode, R7.Pin_1

custom parts:
  Freenove ESP32 GPIO Extension: WS2812B_8_LED_Ring
  Vertical Resistor: A generic resistor (0.25W)
  LED Red 3mm - Top: A generic red LED (~1.8V)
  Vertical Resistor: A generic resistor (0.25W)
