# Fritzing sketch DC Motor L293D ESP32 Example (saved by Fritzing 0.9.9b)
breadboards: 1

parts:
  U1 = ESP32-38PinWide [part_number=ESP32-38PinWide]
  IC1 = L293D [package=THT]
  Part1 = Breadboard Power Supply Board SMD
  M1 = DC Motor

nets:
  N1: U1.GPIO26, IC1.Out_2_(_Controlled_by_Enable_1_)
  N2: U1.GPIO27, IC1.Out_1_(_Controlled_by_Enable_1_)
  N3: U1.GPIO14, IC1.Enable_1
  N4: U1.GPIO11, IC1.0V, Part1.GND
  VIN: U1.VIN, IC1.+Vmotor, IC1.+V, Part1.VCC
  N5: IC1.In_1, M1.pin_2
  N6: IC1.In_2, M1.pin_1

custom parts:
  ESP32-38PinWide: Generic 38-Pin ESP32 with wide format (only access to one side of pins on a breadboard) based on Stephen Lilley's HiLetgo ESP-WROOM-32 ESP32 ESP-32S Development Board.
