# Fritzing sketch DC Motor L293D ESP32 wBOB Example (saved by Fritzing 1.0.6)
breadboards: 1

parts:
  IC1 = L293D [package=THT]  # not connected
  M1 = DC Motor [voltage_(max)=6V voltage_(min)=3V]  # not connected
  Part1 = Freenove ESP32 GPIO Extension
  Part2 = Freenove ESP32 WROVER [package=ESP32-WROVER]  # not connected

nets:
  N1: Part1.GND, Part1.pin_82, Part1.pin_85, Part1.pin_86, Part1.pin_89
  N2: Part1.5V, Part1.pin_83, Part1.pin_84
  N3: Part1.pin_87, Part1.pin_88

custom parts:
  Freenove ESP32 GPIO Extension: WS2812B_8_LED_Ring
