# Fritzing sketch DC Motor L293D Example (saved by Fritzing 0.9.4)
breadboards: 1

parts:
  IC1 = L293D [package=THT]
  M1 = DC Motor
  Part1 = Arduino Uno (Rev3) - ICSP
  VCC1 = Battery block 9V

nets:
  N1: IC1.Enable_1, Part1.D10_PWM/SS
  N2: IC1.In_1, Part1.D9_PWM
  N3: IC1.Out_1_(_Controlled_by_Enable_1_), M1.pin_2
  N4: IC1.0V, Part1.GND, VCC1.-
  N5: IC1.Out_2_(_Controlled_by_Enable_1_), M1.pin_1
  N6: IC1.In_2, Part1.D7
  N7: IC1.+Vmotor, VCC1.+

notes:
  THIS IS ACTUALLY THE BREADBOARD POWER SUPPLY
